# Fritzing sketch ChickenDoor2 (saved by Fritzing 0.9.3b)
breadboards: 1

parts:
  Part1 = Arduino Uno (Rev3)
  Part2 = Arduino Motor Shield (Rev3)
  DHT1 = DHT11 Humitidy and Temperature Sensor

nets:
  GND: Part1.GND, Part2.GND, DHT1.GND
  3V3: Part1.3V3, Part2.3V3
  5V: Part1.5V, Part2.5V, DHT1.VDD
  VIN: Part1.VIN, Part2.VIN
  N1: Part2.D7, DHT1.DATA

custom parts:
  DHT11 Humitidy and Temperature Sensor: DHT11 Humidity and Temperature Sensor
