# Fritzing sketch HUZZAH_temperature_sensor (saved by Fritzing 0.9.3b)
breadboards: 1

parts:
  Adafruit_HUZZAH_ESP8266_Breakout1 = Adafruit HUZZAH ESP8266 Breakout [part_number=2471]
  DHT1 = DHT11 Humitidy and Temperature Sensor
  R1 = Resistor [tolerance=±5% resistance=220 package="0402 [SMD]"]
  VCC1 = 4 x AAA Battery Mount  # not connected

nets:
  N1: Adafruit_HUZZAH_ESP8266_Breakout1.GND, DHT1.NULL
  N2: Adafruit_HUZZAH_ESP8266_Breakout1.V+, R1.Pin_0
  N3: Adafruit_HUZZAH_ESP8266_Breakout1.#12, DHT1.DATA
  N4: Adafruit_HUZZAH_ESP8266_Breakout1.3V, DHT1.VDD

custom parts:
  DHT11 Humitidy and Temperature Sensor: DHT11 Humidity and Temperature Sensor
